# Fritzing sketch solether (saved by Fritzing 0.9.2b)

parts:
  Part1 = Intel Edison Arduinobreakout
  D1 = SOLAR-IXYS [package=solarbit-12x1]
  U1 = LIPO-2000mAh [package=lipo-2000]
  U2 = 2-Channel 5v Relay Shield [package=relay-2ch5v10a]
  X2 = USB Connectors [package=usb-microb]
  X3 = USB Connectors [package=usb-a-s-silk-female]
  X4 = USB Connectors [package=usb-a-s-silk-female]
  D2 = SOLAR-IXYS [package=solarbit-12x1]  # not connected
  D3 = SOLAR-IXYS [package=solarbit-12x1]  # not connected
  D4 = SOLAR-IXYS [package=solarbit-12x1]  # not connected
  D5 = SOLAR-IXYS [package=solarbit-12x1]  # not connected
  D6 = SOLAR-IXYS [package=solarbit-12x1]  # not connected
  D7 = SOLAR-IXYS [package=solarbit-12x1]  # not connected
  D8 = SOLAR-IXYS [package=solarbit-12x1]  # not connected
  D9 = SOLAR-IXYS [package=solarbit-12x1]  # not connected
  D10 = SOLAR-IXYS [package=solarbit-12x1]  # not connected
  D11 = SOLAR-IXYS [package=solarbit-12x1]  # not connected
  D12 = SOLAR-IXYS [package=solarbit-12x1]  # not connected
  D13 = Diode [package=diode-1n4001]

nets:
  N1: Part1.D12/MISO, U2.IN1
  5V: Part1.5V, U2.VCC
  GND: Part1.GND, U2.GND
  N2: D1.A, D13.A
  N3: U1.+, X2.VBUS, X3.VBUS
  GND_2: U1.-, X2.GND, X3.GND
  N4: U2.K2-In, X4.VBUS
  N5: U2.K2-On, X3.D-
  N6: X3.D+, X4.GND

custom parts:
  2-Channel 5v Relay Shield: 2 Channel 5v Relay Shield w. 2x SPD-06VDC-SD-C
